# Fritzing sketch Arduino (saved by Fritzing 0.9.2b)
circuit board: 8.46667cm x 5.64444cm
breadboards: 1

parts:
  Part1 = Arduino Nano (Rev3.0) (ICSP)
  S1 = Pushbutton [package="[SMD]"]
  S2 = Pushbutton [package="[SMD]"]
  Part2 = Bluetooth Mate Silver
  R1 = Resistor [tolerance=±5% resistance=220 package="0402 [SMD]"]
  R2 = Resistor [tolerance=±5% resistance=220 package="0402 [SMD]"]

nets (from the schematic view):
  N1: Part1.D1/TX, Part2.TX_5V
  N2: Part1.D0/RX, Part2.VCC
  N3: Part1.GND, Part2.RTS_5V, Part2.RX_5V, R1.Pin_0, R2.Pin_0
  N4: Part1.D2, Part1.D3, Part1.3V3, S1.Pin_3, S1.Pin_4, S2.Pin_3, S2.Pin_4, R1.Pin_1, R2.Pin_1
  N5: S1.Pin_1, S1.Pin_2
  N6: S2.Pin_1, S2.Pin_2
